# Fritzing sketch milkcarton-1 (saved by Fritzing 0.9.0b)
breadboards: 1

parts:
  U1 = Spark Core (v1.0)
  ADXL335-BB = Triple Axis Accelerometer Breakout - ADXL335

nets:
  N1: U1.A2, U1.3V3
  N2: U1.A3, U1.A6, ADXL335-BB.ZOUT
  N3: U1.A4, ADXL335-BB.YOUT
  N4: U1.A5, U1.VIN, ADXL335-BB.XOUT
  GND: U1.GND, ADXL335-BB.GND
  3.3V: U1.3V3*, ADXL335-BB.VCC

custom parts:
  Spark Core (v1.0): The Spark Core is a tiny Wi-Fi development board that makes it easy to create internet-connected hardware. The Core is all you need to get started; power it over USB and in minutes you'll be controlling LEDs, switches and motors and collecting data from sensors over the internet! It has 8 digital I/O pins, 8 analog I/O pins, 8 PWM pins; UART (Serial), SPI, I2C, and JTAG peripherals available.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
